// Logisim project RISC-V.circ as structural Verilog: 4 circuits, main circuit main
module main (
);

  wire and_1_out, clock_1_out, not_1_out, not_2_out, not_3_out, undriven;
  wire [2:0] funct3;
  wire [4:0] immediate_decoder_1_rd, immediate_decoder_1_rs1, immediate_decoder_1_rs2, multiplexer_1_out,
       multiplexer_2_out;
  wire [6:0] funct7, opcode;
  wire [23:0] bit_extender_1_out, jump_evaluator_1_next_program_counter_value, register_1_q, register_2_q;
  wire [31:0] immediate_decoder_1_j, ram_1_data, ram_2_data, register_3_q, register_4_q, rom_1_data,
       undriven_2;

  Clock clock_1 (.out(clock_1_out));
  and and_1 (and_1_out, clock_1_out, not_2_out);
  not not_1 (not_1_out, clock_1_out);
  not not_2 (not_2_out, not_1_out);
  Register #(.width(24), .trigger("falling")) register_1 (
    .D(register_2_q), .Q(register_1_q), .clk(and_1_out));  // open: en, clr
  Register #(.width(24)) register_2 (
    .D(jump_evaluator_1_next_program_counter_value), .Q(register_2_q), .clk(and_1_out));  // open: en, clr
  not not_3 (not_3_out, clock_1_out);
  jump_evaluator jump_evaluator_1 (
    .next_program_counter_value(jump_evaluator_1_next_program_counter_value),
    .current_program_counter(register_1_q), .relative_J_immediate(immediate_decoder_1_j),
    .ALU_conditional(undriven));
  ROM #(.addrWidth(24), .dataWidth(32)) rom_1 (.addr(register_1_q), .data(rom_1_data));  // open: sel
  immediate_decoder immediate_decoder_1 (
    .in_1(rom_1_data), .rd(immediate_decoder_1_rd), .rs1(immediate_decoder_1_rs1),
    .rs2(immediate_decoder_1_rs2), .funct3(funct3), .funct7(funct7), .J(immediate_decoder_1_j),
    .opcode(opcode));  // open: I, S, B, U
  Multiplexer #(.width(5)) multiplexer_1 (
    .in0(immediate_decoder_1_rd), .in1(immediate_decoder_1_rs1), .out(multiplexer_1_out), .sel(and_1_out));  // open: en
  Multiplexer #(.width(5)) multiplexer_2 (
    .in0(immediate_decoder_1_rd), .in1(immediate_decoder_1_rs2), .out(multiplexer_2_out), .sel(and_1_out));  // open: en
  RAM #(.addrWidth(5), .dataWidth(32), .bus("separate")) ram_1 (
    .addr(multiplexer_1_out), .din(undriven_2), .data(ram_1_data), .clk(and_1_out), .ld(1'b1));  // open: str, sel, clr
  RAM #(.addrWidth(5), .dataWidth(32), .bus("separate")) ram_2 (
    .addr(multiplexer_2_out), .din(undriven_2), .data(ram_2_data), .clk(and_1_out), .ld(1'b1));  // open: str, sel, clr
  Bit_Extender #(.in_width(32), .out_width(24)) bit_extender_1 (.out(bit_extender_1_out));  // open: in
  Register #(.width(32)) register_3 (.D(ram_1_data), .Q(register_3_q));  // open: en, clk, clr
  Register #(.width(32)) register_4 (.D(ram_2_data), .Q(register_4_q));  // open: en, clk, clr
  ALU alu_1 (.input_A(register_3_q), .input_B(register_4_q));
  RAM #(.addrWidth(24), .dataWidth(32), .bus("separate")) ram_3 (.addr(bit_extender_1_out));  // open: din, data, str, sel, clk, ld, clr
endmodule

module immediate_decoder (
  input  [31:0] in_1,
  output [4:0] rd,
  output [4:0] rs1,
  output [6:0] opcode,
  output [4:0] rs2,
  output [2:0] funct3,
  output [6:0] funct7,
  output [31:0] I,
  output [31:0] S,
  output [31:0] B,
  output [31:0] U,
  output [31:0] J
);

  assign I = {{20{in_1[31]}}, in_1[31:20]};  // Bit_Extender bit_extender_1
  assign S = {{20{in_1[31]}}, {in_1[31:25], in_1[11:7]}};  // Bit_Extender bit_extender_2
  assign B = {{19{in_1[31]}}, {in_1[31], in_1[7], in_1[30:25], in_1[11:8], 1'b0}};  // Bit_Extender bit_extender_3
  assign J = {{11{in_1[31]}}, {in_1[31], in_1[19:12], in_1[20], in_1[30:21], 1'b0}};  // Bit_Extender bit_extender_4

  assign funct3 = in_1[14:12];
  assign funct7 = in_1[31:25];
  assign opcode = in_1[6:0];
  assign rd = in_1[11:7];
  assign rs1 = in_1[19:15];
  assign rs2 = in_1[24:20];
  assign U = {in_1[31:12], {12{1'b0}}};
endmodule

module jump_evaluator (
  input  [23:0] current_program_counter,
  input  [31:0] relative_J_immediate,
  input  ALU_conditional,
  output [23:0] next_program_counter_value
);
endmodule

module ALU (
  input  [31:0] input_A,
  input  [31:0] input_B
);
endmodule
